# Fritzing sketch plano configuración Bluetooth (saved by Fritzing 0.9.3b)
breadboards: 1

parts:
  Componente2 = Arduino Uno (Rev3) - ICSP
  Componente4 = Bluetooth HC-05 Macho

nets:
  N1: Componente2.ICSP_MOSI, Componente2.D11_PWM/MOSI, Componente4.RXD
  N2: Componente2.D10_PWM/SS, Componente4.TXD
  5V: Componente2.5V, Componente4.VCC, Componente4.Key
  GND: Componente2.GND, Componente4.GND
