# Fritzing sketch plano leer Bluetooth (saved by Fritzing 0.9.3b)
breadboards: 1

parts:
  Componente2 = Arduino Uno (Rev3) - ICSP  # not connected
  Componente4 = Bluetooth HC-05 Macho
  Componente5 = Arduino Ethernet Shield (Rev3)

nets:
  N1: Componente4.TXD, Componente5.D8
  N2: Componente4.RXD, Componente5.PWM_D9
  VCC: Componente4.VCC, Componente5.5V
  GND: Componente4.Key, Componente4.GND, Componente5.GND
